// Logisim project LED.circ as structural Verilog: 2 circuits, main circuit 7-segment decoder
module _7_segment_decoder (
  input  a3,
  input  a2,
  input  a1,
  input  a0,
  output a,
  output b,
  output c,
  output d,
  output e,
  output f,
  output g
);

  wire and_1_out, and_2_out, and_3_out, and_4_out, and_5_out, and_6_out, and_7_out, and_8_out, and_9_out,
       and_10_out, not_1_out, not_2_out, not_3_out, not_4_out;

  not not_1 (not_1_out, a3);
  not not_2 (not_2_out, a2);
  not not_3 (not_3_out, a1);
  not not_4 (not_4_out, a0);
  and and_1 (and_1_out, not_4_out, not_2_out);
  or or_1 (a, a3, a1, and_2_out, and_1_out);
  and and_2 (and_2_out, a0, a2);
  or or_2 (b, a3, and_4_out, and_3_out, not_2_out);
  and and_3 (and_3_out, not_4_out, not_3_out);
  and and_4 (and_4_out, a0, a1);
  or or_3 (c, a3, a2, a0, and_5_out);
  and and_5 (and_5_out, not_3_out, not_1_out);
  or or_4 (d, a3, and_8_out, and_1_out, and_7_out, and_6_out);
  _7_Segment_Display u_7_segment_display_1 (.g(g), .f(f), .a(a), .b(b), .e(e), .d(d), .c(c));  // open: dp
  and and_6 (and_6_out, not_4_out, a1);
  and and_7 (and_7_out, a1, not_2_out);
  or or_5 (e, and_1_out, and_6_out);
  and and_8 (and_8_out, a0, not_3_out, a2);
  or or_6 (f, a3, and_3_out, and_9_out, and_10_out);
  and and_9 (and_9_out, not_3_out, a2);
  or or_7 (g, a3, and_6_out, and_7_out, and_9_out);
  and and_10 (and_10_out, not_4_out, a2);

  // Notes on the sheet:
  //   a0'a2'
  //   a0a2
  //   a0a1
  //   a0'a1'
  //   a1'a3'
  //   a0'a1
  //   a1a2'
  //   a0a1'a2
  //   a1'a2
  //   a0'a2
endmodule

module main (
  input  in_1,
  input  in_2,
  input  in_3,
  input  in_4
);

  wire n7_segment_decoder_1_a, n7_segment_decoder_1_b, n7_segment_decoder_1_c, n7_segment_decoder_1_d,
       n7_segment_decoder_1_e, n7_segment_decoder_1_f, n7_segment_decoder_1_g;

  _7_segment_decoder u_7_segment_decoder_1 (
    .a3(in_1), .a2(in_2), .a1(in_3), .a0(in_4), .a(n7_segment_decoder_1_a), .b(n7_segment_decoder_1_b),
    .c(n7_segment_decoder_1_c), .d(n7_segment_decoder_1_d), .e(n7_segment_decoder_1_e),
    .f(n7_segment_decoder_1_f), .g(n7_segment_decoder_1_g));
  _7_Segment_Display u_7_segment_display_1 (
    .g(n7_segment_decoder_1_g), .f(n7_segment_decoder_1_f), .a(n7_segment_decoder_1_a),
    .b(n7_segment_decoder_1_b), .e(n7_segment_decoder_1_e), .d(n7_segment_decoder_1_d),
    .c(n7_segment_decoder_1_c));  // open: dp
endmodule
