// Logisim project Vending.circ as structural Verilog: 1 circuit, main circuit main
module main (
);

  wire and_1_out, and_2_out, and_3_out, and_4_out, and_5_out, and_6_out, and_7_out, clock_1_out, Dime_out,
       Nickel_out, not_1_out, not_2_out, or_1_out, or_2_out, or_3_out, s_r_ff_1_q, s_r_ff_1_qn, s_r_ff_2_q,
       s_r_ff_2_qn;

  not not_1 (not_1_out, Nickel_out);
  Button Nickel (.out(Nickel_out));
  Button Dime (.out(Dime_out));
  not not_2 (not_2_out, Dime_out);
  Clock #(.highDuration(1), .lowDuration(1)) clock_1 (.out(clock_1_out));
  or or_1 (or_1_out, Dime_out, and_1_out);
  and and_1 (and_1_out, Nickel_out, s_r_ff_2_q);
  and and_2 (and_2_out, not_2_out, not_1_out, s_r_ff_2_q);
  and and_3 (and_3_out, Nickel_out, s_r_ff_2_qn);
  or or_2 (or_2_out, and_3_out, and_4_out);
  and and_4 (and_4_out, Dime_out, s_r_ff_1_q);
  and and_5 (and_5_out, Nickel_out, s_r_ff_1_qn, s_r_ff_2_q);
  or or_3 (or_3_out, and_5_out, and_6_out);
  and and_6 (and_6_out, not_1_out, not_2_out, s_r_ff_1_q);
  S_R_Flip_Flop s_r_ff_1 (
    .S(or_1_out), .clk(clock_1_out), .R(and_2_out), .Q(s_r_ff_1_q), .Qn(s_r_ff_1_qn));  // open: preset, reset, en
  S_R_Flip_Flop s_r_ff_2 (
    .S(or_2_out), .clk(clock_1_out), .R(or_3_out), .Q(s_r_ff_2_q), .Qn(s_r_ff_2_qn));  // open: preset, reset, en
  and and_7 (and_7_out, not_1_out, not_2_out, s_r_ff_1_q, s_r_ff_2_q);
  LED Product (.in(and_7_out));

  // Notes on the sheet:
  //   A
  //   B
endmodule
