// Logisim project finalHmwk.circ as structural Verilog: 1 circuit, main circuit main
module main (
  input  in_1,
  input  in_2,
  output a,
  output b,
  output c,
  output d,
  output e,
  output f,
  output g
);

  wire and_1_out, and_2_out, and_3_out, and_4_out, and_5_out, and_6_out, and_7_out, and_8_out, and_9_out,
       and_10_out, and_11_out, and_12_out, and_13_out, clock_1_out, j_k_ff_1_q, j_k_ff_2_q, j_k_ff_3_q,
       not_1_out, not_2_out, not_3_out, not_4_out, not_5_out, not_6_out, or_1_out, or_2_out, or_3_out;

  not not_1 (not_1_out, j_k_ff_3_q);
  not not_2 (not_2_out, j_k_ff_2_q);
  not not_3 (not_3_out, j_k_ff_3_q);
  and and_1 (and_1_out, in_1, not_1_out, not_2_out);
  and and_2 (and_2_out, j_k_ff_2_q, j_k_ff_3_q, in_2);
  and and_3 (and_3_out, in_1, not_3_out);
  and and_4 (and_4_out, in_2, j_k_ff_3_q);
  or or_1 (or_1_out, and_1_out, and_2_out);
  or or_2 (or_2_out, and_3_out, and_4_out);
  or or_3 (or_3_out, in_1, in_2);
  Clock #(.highDuration(1), .lowDuration(1)) clock_1 (.out(clock_1_out));
  J_K_Flip_Flop j_k_ff_1 (
    .J(or_1_out), .clk(clock_1_out), .K(or_1_out), .Q(j_k_ff_1_q));  // open: Qn, preset, en, reset
  J_K_Flip_Flop j_k_ff_2 (
    .J(or_2_out), .clk(clock_1_out), .K(or_2_out), .Q(j_k_ff_2_q));  // open: Qn, preset, en, reset
  J_K_Flip_Flop j_k_ff_3 (
    .J(or_3_out), .clk(clock_1_out), .K(or_3_out), .Q(j_k_ff_3_q));  // open: Qn, preset, en, reset
  not not_4 (not_4_out, j_k_ff_1_q);
  not not_5 (not_5_out, j_k_ff_2_q);
  not not_6 (not_6_out, j_k_ff_3_q);
  and and_5 (and_5_out, not_6_out, not_4_out);
  or or_4 (a, j_k_ff_2_q, and_6_out, and_5_out);
  and and_6 (and_6_out, j_k_ff_3_q, j_k_ff_1_q);
  or or_5 (b, and_7_out, and_8_out, not_4_out);
  and and_7 (and_7_out, not_6_out, not_5_out);
  and and_8 (and_8_out, j_k_ff_3_q, j_k_ff_2_q);
  or or_6 (c, j_k_ff_1_q, j_k_ff_3_q, not_5_out);
  _7_Segment_Display u_7_segment_display_1 (.g(g), .f(f), .a(a), .b(b), .e(e), .d(d), .c(c));  // open: dp
  or or_7 (d, and_11_out, and_5_out, and_10_out, and_9_out);
  and and_9 (and_9_out, not_6_out, j_k_ff_2_q);
  or or_8 (e, and_5_out, and_9_out);
  and and_10 (and_10_out, j_k_ff_2_q, not_4_out);
  and and_11 (and_11_out, j_k_ff_3_q, not_5_out, j_k_ff_1_q);
  or or_9 (f, and_7_out, and_12_out, and_13_out);
  and and_12 (and_12_out, not_5_out, j_k_ff_1_q);
  and and_13 (and_13_out, not_6_out, j_k_ff_1_q);
  or or_10 (g, and_9_out, and_10_out, and_12_out);

  // Notes on the sheet:
  //   a0'a2'
  //   a0a2
  //   a0'a1'
  //   a0a1
  //   a0'a1
  //   a1a2'
  //   a0a1'a2
  //   a1'a2
  //   a0'a2
endmodule
